# Fritzing sketch indoorsensing_circuit (saved by Fritzing 0.9.3b)
breadboards: 1

parts:
  U1 = NodeMCU V1.0
  PIR1 = PIR sensor
  DHT1 = DHT11 Humitidy and Temperature Sensor
  Squix1 = OLED 0.96" 128x64 I2C SSD1306
  LED1 = LED - 3mm [color="Red (633nm)" package="3 mm [THT]"]

nets:
  N1: U1.D1, Squix1.SCL
  N2: U1.D2, Squix1.SCA
  N3: U1.D3, PIR1.SIG
  N4: U1.D4, DHT1.DATA
  N5: U1.D5, LED1.cathode
  GND: U1.GND, PIR1.GND, DHT1.NULL, DHT1.GND, Squix1.GND, LED1.anode
  VDD: U1.3V3, PIR1.VDD, DHT1.VDD, Squix1.VCC

custom parts:
  NodeMCU V1.0: ESP8266 based NodeMCU
  DHT11 Humitidy and Temperature Sensor: DHT11 Humidity and Temperature Sensor
