# Fritzing sketch rpi (saved by Fritzing 0.9.3b)

parts:
  Raspberry_Pi_1 = Raspberry Pi 3 [part_number=RPI-3-V1.2]
  LED1 = smd LED [color="Red (633nm)" package="0805 [SMD]"]
  LED2 = smd LED [color="Red (633nm)" package="0805 [SMD]"]
  LCD2 = LCD screen
  LCM1602_IIC1 = LCM1602 IIC [part_number="LCM1602 IIC" chip_label="LCM1602 IIC" package="DIP (Dual Inline) [THT]"]
  R1 = Resistor [tolerance=±5% resistance=82 package="0402 [SMD]"]
  R2 = Resistor [tolerance=±5% resistance=82 package="0402 [SMD]"]

nets:
  N1: Raspberry_Pi_1.GPIO2, LCM1602_IIC1.SDA
  N2: Raspberry_Pi_1.GPIO3, LCM1602_IIC1.SCL
  GND: Raspberry_Pi_1.GND, LCM1602_IIC1.GND, R1.Pin_1, R2.Pin_1
  N3: Raspberry_Pi_1.GIPO16, LED2.anode
  5V: Raspberry_Pi_1.5V, LED1.anode, LCM1602_IIC1.VCC
  N4: LED1.cathode, R1.Pin_0
  N5: LED2.cathode, R2.Pin_0
  VSS: LCD2.VSS, LCM1602_IIC1.VSS
  VDD: LCD2.VDD, LCM1602_IIC1.VDD
  N6: LCD2.V0, LCM1602_IIC1.V0
  N7: LCD2.RS, LCM1602_IIC1.RS
  N8: LCD2.R/W, LCM1602_IIC1.RW
  N9: LCD2.E, LCM1602_IIC1.E
  N10: LCD2.DB0, LCM1602_IIC1.D0
  N11: LCD2.DB1, LCM1602_IIC1.D1
  N12: LCD2.DB2, LCM1602_IIC1.D2
  N13: LCD2.DB3, LCM1602_IIC1.D3
  N14: LCD2.DB4, LCM1602_IIC1.D4
  N15: LCD2.DB5, LCM1602_IIC1.D5
  N16: LCD2.DB6, LCM1602_IIC1.D6
  N17: LCD2.DB7, LCM1602_IIC1.D7
  N18: LCD2.LED+, LCM1602_IIC1.A
  N19: LCD2.LED-, LCM1602_IIC1.K
  N20: LCM1602_IIC1.LED_A, LCM1602_IIC1.LED_B

custom parts:
  LCM1602 IIC: I2C-Module to use a 1602 or 2004 LCD on with the wire.h libory Serial LCD Modul
